// Logisim project RISC V.circ as structural Verilog: 14 circuits, main circuit main
module main (
  input  in_1,
  output [31:0] out_2,
  output [2:0] out_3,
  output [31:0] out_4,
  output [31:0] out_5,
  output [31:0] out_6,
  output [31:0] out_7,
  output [11:0] out_8,
  output [31:0] out_9,
  output [31:0] out_10,
  output [3:0] out_11,
  output [31:0] out_12,
  output [31:0] out_13,
  output [31:0] out_14,
  output [31:0] out_15,
  output [4:0] out_16,
  output [4:0] out_17,
  output [4:0] out_18,
  output [31:0] out_19
);

  wire branch_sel_1_out_4, clock_1_out, clock_2_out, control_1_out_4, control_1_out_6, control_1_out_7,
       control_1_out_9, or_1_out;
  wire [1:0] control_1_out_8, IMM_SEL, NEXT_PC;
  wire [2:0] FN_3;
  wire [31:0] imm_gen_1_out_3, imm_gen_1_out_4, imm_gen_1_out_7, multiplexer_2_out, multiplexer_3_out,
       ram_1_data, SB, UJ;

  Clock clock_1 (.out(clock_1_out));
  Register #(.width(32)) register_1 (.D(out_2), .Q(out_7), .clk(clock_1_out), .clr(in_1));  // open: en
  Multiplexer #(.select(2), .width(32)) multiplexer_1 (
    .in0(out_6), .in1(out_19), .in2(UJ), .in3(multiplexer_2_out), .out(out_2), .sel(NEXT_PC));  // open: en
  Adder #(.width(32)) adder_1 (.a(out_7), .b(32'h4), .out(out_6));  // open: cin, cout
  Multiplexer #(.width(32), .enable("false")) multiplexer_2 (
    .in0(out_6), .in1(SB), .out(multiplexer_2_out), .sel(branch_sel_1_out_4));
  BRANCH_SEL branch_sel_1 (.in_3(FN_3), .out_4(branch_sel_1_out_4), .in_1(out_13), .in_2(out_12));
  ROM #(.addrWidth(12), .dataWidth(32)) rom_1 (
    .addr(out_7[13:2]), .data({out_15[31:15], out_3, out_15[11:0]}));  // open: sel
  CONTROL control_1 (
    .OP_CODE(out_15[6:0]), .out_4(control_1_out_4), .out_6(control_1_out_6), .out_7(control_1_out_7),
    .out_8(control_1_out_8), .out_9(control_1_out_9), .out_10(IMM_SEL), .out_11(NEXT_PC), .out_12(out_11),
    .in_2(out_3), .in_3(out_15[30]));  // open: out_5
  REGISTER register_2 (
    .out_7(out_13), .out_8(out_12), .in_1(out_10), .in_3(control_1_out_4), .in_4(out_15[11:7]),
    .in_2(out_15[19:15]), .in_5(out_15[24:20]));  // open: in_6
  IMM_GEN imm_gen_1 (
    .in_1({out_15[31:15], out_3, out_15[11:0]}), .in_2(out_7), .out_3(imm_gen_1_out_3),
    .out_4(imm_gen_1_out_4), .out_5(SB), .out_6(UJ), .out_7(imm_gen_1_out_7));
  Multiplexer #(.select(2), .width(32)) multiplexer_3 (
    .in0(imm_gen_1_out_3), .in1(imm_gen_1_out_7), .in2(imm_gen_1_out_4), .out(multiplexer_3_out),
    .sel(IMM_SEL));  // open: in3, en
  Multiplexer #(.select(2), .width(32), .enable("false")) multiplexer_4 (
    .in0(out_13), .in1(out_7), .in2(out_6), .in3({32{1'b0}}), .out(out_4), .sel(control_1_out_8));
  Multiplexer #(.width(32), .enable("false")) multiplexer_5 (
    .in0(out_12), .in1(multiplexer_3_out), .out(out_5), .sel(control_1_out_9));
  Adder #(.width(32)) adder_2 (.a(out_13), .b(imm_gen_1_out_3), .out(out_19));  // open: cin, cout
  ALU alu_1 (
    .Operand_A(out_4), .Operand_B(out_5), .ALU_out({out_9[31:14], out_8, out_9[1:0]}), .Alu_Out_Select(out_11));  // open: Overflow
  or or_1 (or_1_out, control_1_out_6, control_1_out_7);
  Clock clock_2 (.out(clock_2_out));
  RAM #(.addrWidth(12), .dataWidth(32), .bus("separate")) ram_1 (
    .addr(out_8), .din(out_12), .data(ram_1_data), .str(control_1_out_6), .sel(or_1_out), .clk(clock_2_out),
    .ld(control_1_out_7), .clr(in_1));
  Multiplexer #(.width(32), .enable("false")) multiplexer_6 (
    .in0(ram_1_data), .in1({out_9[31:14], out_8, out_9[1:0]}), .out(out_10), .sel(control_1_out_7));

  assign out_9[13:2] = out_8;
  assign out_14 = out_10;
  assign out_15[14:12] = out_3;
  assign out_16 = out_15[11:7];
  assign out_17 = out_15[24:20];
  assign out_18 = out_15[19:15];

  // Other names for the same wires on the sheet: A[31:0] = out_13; ALU[3:0] = out_11; B[31:0] = out_12; CL = in_1;
  //   JALR[31:0] = out_19; FN3[2:0] = out_3; WD[31:0] = out_10

  // Notes on the sheet:
  //   contents of rom_1 (hex, n*v repeats v):
  //   a00113 1e00293 22e333 22f3b3 22c433 a2c493 22a533 1e12593 229613 22d613
endmodule

module NEXT_PC (
  input  SB,
  input  JAL,
  input  JALR,
  output A,
  output B
);

  or or_1 (A, JALR, SB);
  or or_2 (B, JAL, SB);
endmodule

module CONTROL_DECODE (
  input  R_Type,
  input  I_Type,
  input  Load,
  input  JALR,
  input  Store,
  input  Branch,
  input  Auipc,
  input  Lui,
  input  JAL,
  input  [2:0] FN_3,
  input  FN_7,
  output REG_Write,
  output Branch_2,
  output Store_2,
  output Mem_2_Reg,
  output [1:0] OPERAND_A,
  output OPERAND_B,
  output [1:0] IMM_SELECTOR,
  output [1:0] NEXT_PC,
  output OUT_0,
  output OUT_1,
  output OUT_2,
  output OUT_3
);

  wire alu_c_1_alu_0, alu_c_1_alu_1, alu_c_1_alu_2, or_1_out, or_2_out, or_3_out, or_4_out;

  or or_1 (or_1_out, JALR, Load, I_Type);
  or or_2 (or_2_out, or_1_out, R_Type, Store, Branch);
  or or_3 (or_3_out, Branch, Auipc);
  or or_4 (or_4_out, JAL, JALR);
  or or_5 (OPERAND_B, R_Type, Branch, Store);
  or or_6 (REG_Write, R_Type, I_Type, Load, JALR, Auipc, Lui, JAL);
  OPERAND_A operand_a_1 (
    .JAL_JALR(or_4_out), .AUIPC(Auipc), .ZERO(1'b0), .REG_1(or_2_out), .output_0(OPERAND_A[1]),
    .output_1(OPERAND_A[0]));
  IMM_SELECTOR imm_selector_1 (.STYPE(Store), .UTYPE(or_3_out), .a(IMM_SELECTOR[1]), .b(IMM_SELECTOR[0]));
  NEXT_PC next_pc_1 (.SB(Store), .JAL(JAL), .JALR(JALR), .A(NEXT_PC[1]), .B(NEXT_PC[0]));
  ALU_C alu_c_1 (
    .R_TYPE(R_Type), .I_TYPE(I_Type), .LOAD(Load), .JALR(JALR), .STORE(Store), .AUIPC(Auipc), .LUI(Lui),
    .JAL(JAL), .ALU_0(alu_c_1_alu_0), .ALU_1(alu_c_1_alu_1), .ALU_2(alu_c_1_alu_2));
  ALU_CONTROL alu_control_1 (
    .ALU_OP_0(alu_c_1_alu_0), .ALU_OP_1(alu_c_1_alu_1), .ALU_OP_2(alu_c_1_alu_2), .FN_3_0(FN_3[0]),
    .FN_3_1(FN_3[1]), .FN_3_2(FN_3[2]), .FN_7(FN_7), .ALU_SEL_0(OUT_0), .ALU_SEL_1(OUT_1), .ALU_SEL_2(OUT_2),
    .ALU_SEL_3(OUT_3));

  assign Branch_2 = Branch;
  assign Mem_2_Reg = Load;
  assign Store_2 = Store;
endmodule

module OPERAND_A (
  input  JAL_JALR,
  input  AUIPC,
  input  ZERO,
  input  REG_1,
  output output_0,
  output output_1
);

  wire not_1_out, not_2_out, not_3_out, not_4_out;

  not not_1 (not_1_out, JAL_JALR);
  and and_1 (output_0, not_1_out, not_2_out);
  not not_2 (not_2_out, REG_1);
  not not_3 (not_3_out, AUIPC);
  and and_2 (output_1, not_3_out, not_4_out);
  not not_4 (not_4_out, REG_1);
endmodule

module IMM_SELECTOR (
  input  STYPE,
  input  UTYPE,
  output a,
  output b
);

  not not_1 (a, STYPE);
  not not_2 (b, UTYPE);
endmodule

module ALU_C (
  input  R_TYPE,
  input  I_TYPE,
  input  LOAD,
  input  JALR,
  input  STORE,
  input  AUIPC,
  input  LUI,
  input  JAL,
  output ALU_0,
  output ALU_1,
  output ALU_2
);

  wire or_1_out, or_2_out, or_3_out, or_4_out, or_5_out, or_6_out;

  or or_1 (or_1_out, JAL, LUI);
  or or_2 (or_2_out, AUIPC, STORE);
  or or_3 (or_3_out, JAL, LUI);
  or or_4 (or_4_out, JALR, LOAD);
  or or_5 (or_5_out, JAL, AUIPC);
  or or_6 (or_6_out, JALR, I_TYPE);
  or or_7 (ALU_0, or_1_out, or_2_out);
  or or_8 (ALU_1, or_3_out, or_4_out);
  or or_9 (ALU_2, or_5_out, or_6_out);
endmodule

module ALU_CONTROL (
  input  ALU_OP_0,
  input  ALU_OP_1,
  input  ALU_OP_2,
  input  FN_3_0,
  input  FN_3_1,
  input  FN_3_2,
  input  FN_7,
  output ALU_SEL_0,
  output ALU_SEL_1,
  output ALU_SEL_2,
  output ALU_SEL_3
);

  wire and_1_out, and_2_out, and_3_out, and_4_out, and_5_out, and_6_out, and_7_out, and_8_out, and_9_out,
       and_10_out, and_11_out, and_12_out, and_13_out, and_14_out, and_15_out, and_16_out, and_17_out,
       and_18_out, and_19_out, and_20_out, and_21_out, and_22_out, and_23_out, and_24_out, and_25_out,
       and_26_out, and_27_out, and_28_out, and_29_out, and_30_out, and_31_out, and_32_out, and_33_out,
       and_34_out, and_35_out, and_36_out, and_37_out, and_38_out, and_39_out, and_40_out, and_41_out,
       and_42_out, and_43_out, and_44_out, and_45_out, and_46_out, and_47_out, not_1_out, not_2_out,
       not_3_out, not_4_out, not_5_out, not_6_out, not_7_out, not_8_out, not_9_out, not_10_out, not_11_out,
       not_12_out, not_13_out, not_14_out, not_15_out, not_16_out, not_17_out, not_18_out, not_19_out,
       not_20_out, not_21_out, not_22_out, not_23_out, not_24_out, not_25_out, not_26_out, not_27_out,
       not_28_out, not_29_out, not_30_out, not_31_out, not_32_out, not_33_out, not_34_out, not_35_out,
       not_36_out, or_1_out, or_2_out, or_3_out, or_4_out, or_5_out, or_6_out, or_7_out, or_8_out, or_10_out,
       or_11_out, or_12_out, or_13_out, or_14_out, or_15_out;

  not not_1 (not_1_out, ALU_OP_1);
  not not_2 (not_2_out, FN_3_0);
  not not_3 (not_3_out, ALU_OP_2);
  not not_4 (not_4_out, FN_3_1);
  not not_5 (not_5_out, ALU_OP_0);
  not not_6 (not_6_out, FN_3_0);
  not not_7 (not_7_out, ALU_OP_0);
  not not_8 (not_8_out, ALU_OP_1);
  not not_9 (not_9_out, FN_3_1);
  not not_10 (not_10_out, FN_3_2);
  not not_11 (not_11_out, ALU_OP_1);
  not not_12 (not_12_out, FN_3_1);
  not not_13 (not_13_out, FN_7);
  not not_14 (not_14_out, ALU_OP_1);
  not not_15 (not_15_out, ALU_OP_2);
  not not_16 (not_16_out, FN_3_0);
  not not_17 (not_17_out, ALU_OP_1);
  not not_18 (not_18_out, ALU_OP_2);
  not not_19 (not_19_out, FN_3_0);
  not not_20 (not_20_out, ALU_OP_0);
  not not_21 (not_21_out, FN_3_0);
  not not_22 (not_22_out, ALU_OP_0);
  and and_1 (and_1_out, not_1_out, FN_3_0);
  not not_23 (not_23_out, FN_3_1);
  and and_2 (and_2_out, ALU_OP_1, not_2_out);
  not not_24 (not_24_out, FN_7);
  and and_3 (and_3_out, not_3_out, not_4_out);
  and and_4 (and_4_out, not_5_out, not_6_out);
  and and_5 (and_5_out, not_7_out, FN_3_2);
  and and_6 (and_6_out, not_8_out, not_9_out);
  and and_7 (and_7_out, not_10_out, FN_7);
  and and_8 (and_8_out, not_11_out, FN_3_0);
  and and_9 (and_9_out, not_12_out, not_13_out);
  not not_25 (not_25_out, ALU_OP_2);
  not not_26 (not_26_out, ALU_OP_1);
  and and_10 (and_10_out, not_14_out, not_15_out);
  and and_11 (and_11_out, not_16_out, FN_7);
  and and_12 (and_12_out, not_17_out, FN_3_1);
  not not_27 (not_27_out, ALU_OP_1);
  not not_28 (not_28_out, FN_3_1);
  not not_29 (not_29_out, FN_3_2);
  and and_13 (and_13_out, ALU_OP_2, FN_3_0);
  not not_30 (not_30_out, FN_3_2);
  not not_31 (not_31_out, ALU_OP_0);
  and and_14 (and_14_out, not_18_out, not_19_out);
  and and_15 (and_15_out, not_20_out, not_21_out);
  and and_16 (and_16_out, not_22_out, FN_3_0);
  not not_32 (not_32_out, FN_3_1);
  and and_17 (and_17_out, and_1_out, not_23_out);
  and and_18 (and_18_out, FN_3_2, FN_7);
  not not_33 (not_33_out, ALU_OP_2);
  and and_19 (and_19_out, and_2_out, FN_3_1);
  and and_20 (and_20_out, FN_3_2, not_24_out);
  and and_21 (and_21_out, and_3_out, FN_7);
  and and_22 (and_22_out, and_4_out, FN_3_2);
  and and_23 (and_23_out, and_5_out, FN_7);
  and and_24 (and_24_out, ALU_OP_0, ALU_OP_1);
  and and_25 (and_25_out, and_6_out, and_7_out);
  and and_26 (and_26_out, and_8_out, and_9_out);
  and and_27 (and_27_out, not_25_out, FN_3_0);
  not not_34 (not_34_out, FN_3_2);
  and and_28 (and_28_out, ALU_OP_0, not_26_out);
  and and_29 (and_29_out, ALU_OP_0, ALU_OP_1);
  not not_35 (not_35_out, ALU_OP_2);
  and and_30 (and_30_out, and_10_out, and_11_out);
  and and_31 (and_31_out, and_12_out, FN_3_2);
  and and_32 (and_32_out, not_27_out, FN_3_0);
  and and_33 (and_33_out, not_28_out, not_29_out);
  and and_34 (and_34_out, and_13_out, not_30_out);
  and and_35 (and_35_out, not_31_out, ALU_OP_1);
  and and_36 (and_36_out, and_14_out, FN_7);
  and and_37 (and_37_out, and_15_out, FN_3_1);
  and and_38 (and_38_out, and_16_out, not_32_out);
  and and_39 (and_39_out, and_17_out, and_18_out);
  and and_40 (and_40_out, ALU_OP_1, not_33_out);
  and and_41 (and_41_out, and_19_out, and_20_out);
  not not_36 (not_36_out, ALU_OP_2);
  or or_1 (or_1_out, and_21_out, and_22_out);
  or or_2 (or_2_out, and_23_out, and_24_out);
  or or_3 (or_3_out, and_25_out, and_26_out);
  and and_42 (and_42_out, and_27_out, not_34_out);
  and and_43 (and_43_out, and_28_out, ALU_OP_2);
  and and_44 (and_44_out, and_29_out, not_35_out);
  or or_4 (or_4_out, and_30_out, and_31_out);
  and and_45 (and_45_out, and_32_out, and_33_out);
  or or_5 (or_5_out, and_34_out, and_35_out);
  and and_46 (and_46_out, ALU_OP_0, ALU_OP_2);
  or or_6 (or_6_out, and_36_out, and_37_out);
  or or_7 (or_7_out, and_38_out, and_39_out);
  or or_8 (or_8_out, and_40_out, and_41_out);
  and and_47 (and_47_out, ALU_OP_0, not_36_out);
  or or_9 (ALU_SEL_1, or_1_out, or_2_out);
  or or_10 (or_10_out, or_3_out, and_42_out);
  or or_11 (or_11_out, and_43_out, and_44_out);
  or or_12 (or_12_out, or_4_out, and_45_out);
  or or_13 (or_13_out, or_5_out, and_46_out);
  or or_14 (or_14_out, or_6_out, or_7_out);
  or or_15 (or_15_out, or_8_out, and_47_out);
  or or_16 (ALU_SEL_2, or_10_out, or_11_out);
  or or_17 (ALU_SEL_3, or_12_out, or_13_out);
  or or_18 (ALU_SEL_0, or_14_out, or_15_out);
endmodule

module IMM_GEN (
  input  [31:0] in_1,
  input  [31:0] in_2,
  output [31:0] out_3,
  output [31:0] out_4,
  output [31:0] out_5,
  output [31:0] out_6,
  output [31:0] out_7
);

  wire [19:0] shifter_1_out;
  wire [31:0] bit_extender_3_out, bit_extender_4_out;

  Shifter #(.width(20)) shifter_1 (.in(in_1[31:12]), .\dist (5'b01100), .out(shifter_1_out));
  assign out_3 = {{20{in_1[31]}}, in_1[31:20]};  // Bit_Extender bit_extender_1
  assign out_4 = {{20{in_1[31]}}, {in_1[31:25], in_1[11:7]}};  // Bit_Extender bit_extender_2
  assign bit_extender_3_out = {{19{in_1[31]}}, {in_1[31], in_1[7], in_1[30:25], in_1[11:8], 1'b0}};  // Bit_Extender bit_extender_3
  assign bit_extender_4_out = {{11{in_1[31]}}, {in_1[31], in_1[19:12], in_1[20], in_1[30:21], 1'b0}};  // Bit_Extender bit_extender_4
  assign out_7 = {{12{shifter_1_out[19]}}, shifter_1_out};  // Bit_Extender bit_extender_5
  Adder #(.width(32)) adder_1 (.a(bit_extender_3_out), .b(in_2), .out(out_5));  // open: cin, cout
  Adder #(.width(32)) adder_2 (.a(bit_extender_4_out), .b(in_2), .out(out_6));  // open: cin, cout
endmodule

module TYPE_DECODE (
  input  [6:0] in_1,
  output R_TYPE,
  output I_TYPE,
  output LOAD,
  output JALR,
  output STORE,
  output BRANCH,
  output AUIPC,
  output LUI,
  output JAL
);

  Comparator #(.width(7)) comparator_1 (.a(in_1), .b(7'b0110011), .eq(R_TYPE));  // open: gt, lt
  Comparator #(.width(7)) comparator_2 (.a(in_1), .b(7'b0010011), .eq(I_TYPE));  // open: gt, lt
  Comparator #(.width(7)) comparator_3 (.a(in_1), .b(7'b0000011), .eq(LOAD));  // open: gt, lt
  Comparator #(.width(7)) comparator_4 (.a(in_1), .b(7'b1100111), .eq(JALR));  // open: gt, lt
  Comparator #(.width(7)) comparator_5 (.a(in_1), .b(7'b0100011), .eq(STORE));  // open: gt, lt
  Comparator #(.width(7)) comparator_6 (.a(in_1), .b(7'b1100011), .eq(BRANCH));  // open: gt, lt
  Comparator #(.width(7)) comparator_7 (.a(in_1), .b(7'b0010111), .eq(AUIPC));  // open: gt, lt
  Comparator #(.width(7)) comparator_8 (.a(in_1), .b(7'b0110111), .eq(LUI));  // open: gt, lt
  Comparator #(.width(7)) comparator_9 (.a(in_1), .b(7'b1101111), .eq(JAL));  // open: gt, lt
endmodule

module REGISTER (
  input  [31:0] in_1,
  input  [4:0] in_2,
  input  in_3,
  input  [4:0] in_4,
  input  [4:0] in_5,
  input  in_6,
  output [31:0] out_7,
  output [31:0] out_8
);

  wire decoder_1_out0, decoder_1_out1, decoder_1_out2, decoder_1_out3, decoder_1_out4, decoder_1_out5,
       decoder_1_out6, decoder_1_out7, decoder_1_out8, decoder_1_out9, decoder_1_out10, decoder_1_out11,
       decoder_1_out12, decoder_1_out13, decoder_1_out14, decoder_1_out15, decoder_1_out16, decoder_1_out17,
       decoder_1_out18, decoder_1_out19, decoder_1_out20, decoder_1_out21, decoder_1_out22, decoder_1_out23,
       decoder_1_out24, decoder_1_out25, decoder_1_out26, decoder_1_out27, decoder_1_out28, decoder_1_out29,
       decoder_1_out30;
  wire [31:0] REGISTER_2_q, REGISTER_3_q, REGISTER_4_q, REGISTER_5_q, REGISTER_6_q, REGISTER_7_q,
       REGISTER_8_q, REGISTER_9_q, REGISTER_10_q, REGISTER_11_q, REGISTER_12_q, REGISTER_13_q, REGISTER_14_q,
       REGISTER_15_q, REGISTER_16_q, REGISTER_17_q, REGISTER_18_q, REGISTER_19_q, REGISTER_20_q,
       REGISTER_21_q, REGISTER_22_q, REGISTER_23_q, REGISTER_24_q, REGISTER_25_q, REGISTER_26_q,
       REGISTER_27_q, REGISTER_28_q, REGISTER_29_q, REGISTER_30_q, REGISTER_31_q, REGISTER_32_q;

  Decoder #(.select(5)) decoder_1 (
    .out0(decoder_1_out0), .out1(decoder_1_out1), .out2(decoder_1_out2), .out3(decoder_1_out3),
    .out4(decoder_1_out4), .out5(decoder_1_out5), .out6(decoder_1_out6), .out7(decoder_1_out7),
    .out8(decoder_1_out8), .out9(decoder_1_out9), .out10(decoder_1_out10), .out11(decoder_1_out11),
    .out12(decoder_1_out12), .out13(decoder_1_out13), .out14(decoder_1_out14), .out15(decoder_1_out15),
    .out16(decoder_1_out16), .out17(decoder_1_out17), .out18(decoder_1_out18), .out19(decoder_1_out19),
    .out20(decoder_1_out20), .out21(decoder_1_out21), .out22(decoder_1_out22), .out23(decoder_1_out23),
    .out24(decoder_1_out24), .out25(decoder_1_out25), .out26(decoder_1_out26), .out27(decoder_1_out27),
    .out28(decoder_1_out28), .out29(decoder_1_out29), .out30(decoder_1_out30), .sel(in_4), .en(in_3));  // open: out31
  Register #(.width(32)) REGISTER_2 (.D(in_1), .en(decoder_1_out0), .Q(REGISTER_2_q), .clk(in_6));  // open: clr
  Register #(.width(32)) REGISTER_3 (.D(in_1), .en(decoder_1_out1), .Q(REGISTER_3_q), .clk(in_6));  // open: clr
  Register #(.width(32)) REGISTER_4 (.D(in_1), .en(decoder_1_out2), .Q(REGISTER_4_q), .clk(in_6));  // open: clr
  Register #(.width(32)) REGISTER_5 (.D(in_1), .en(decoder_1_out3), .Q(REGISTER_5_q), .clk(in_6));  // open: clr
  Register #(.width(32)) REGISTER_6 (.D(in_1), .en(decoder_1_out4), .Q(REGISTER_6_q), .clk(in_6));  // open: clr
  Register #(.width(32)) REGISTER_7 (.D(in_1), .en(decoder_1_out5), .Q(REGISTER_7_q), .clk(in_6));  // open: clr
  Register #(.width(32)) REGISTER_8 (.D(in_1), .en(decoder_1_out6), .Q(REGISTER_8_q), .clk(in_6));  // open: clr
  Register #(.width(32)) REGISTER_9 (.D(in_1), .en(decoder_1_out7), .Q(REGISTER_9_q), .clk(in_6));  // open: clr
  Register #(.width(32)) REGISTER_10 (.D(in_1), .en(decoder_1_out8), .Q(REGISTER_10_q), .clk(in_6));  // open: clr
  Register #(.width(32)) REGISTER_11 (.D(in_1), .en(decoder_1_out9), .Q(REGISTER_11_q), .clk(in_6));  // open: clr
  Register #(.width(32)) REGISTER_12 (.D(in_1), .en(decoder_1_out10), .Q(REGISTER_12_q), .clk(in_6));  // open: clr
  Register #(.width(32)) REGISTER_13 (.D(in_1), .en(decoder_1_out11), .Q(REGISTER_13_q), .clk(in_6));  // open: clr
  Register #(.width(32)) REGISTER_14 (.D(in_1), .en(decoder_1_out12), .Q(REGISTER_14_q), .clk(in_6));  // open: clr
  Register #(.width(32)) REGISTER_15 (.D(in_1), .en(decoder_1_out13), .Q(REGISTER_15_q));  // open: clk, clr
  Register #(.width(32)) REGISTER_16 (.D(in_1), .en(decoder_1_out14), .Q(REGISTER_16_q), .clk(in_6));  // open: clr
  Register #(.width(32)) REGISTER_17 (.D(in_1), .en(decoder_1_out15), .Q(REGISTER_17_q), .clk(in_6));  // open: clr
  Register #(.width(32)) REGISTER_18 (.D(in_1), .en(decoder_1_out16), .Q(REGISTER_18_q), .clk(in_6));  // open: clr
  Register #(.width(32)) REGISTER_19 (.D(in_1), .en(decoder_1_out17), .Q(REGISTER_19_q), .clk(in_6));  // open: clr
  Register #(.width(32)) REGISTER_20 (.D(in_1), .en(decoder_1_out18), .Q(REGISTER_20_q), .clk(in_6));  // open: clr
  Register #(.width(32)) REGISTER_21 (.D(in_1), .en(decoder_1_out19), .Q(REGISTER_21_q), .clk(in_6));  // open: clr
  Register #(.width(32)) REGISTER_22 (.D(in_1), .en(decoder_1_out20), .Q(REGISTER_22_q), .clk(in_6));  // open: clr
  Register #(.width(32)) REGISTER_23 (.D(in_1), .en(decoder_1_out21), .Q(REGISTER_23_q), .clk(in_6));  // open: clr
  Register #(.width(32)) REGISTER_24 (.D(in_1), .en(decoder_1_out22), .Q(REGISTER_24_q), .clk(in_6));  // open: clr
  Register #(.width(32)) REGISTER_25 (.D(in_1), .en(decoder_1_out23), .Q(REGISTER_25_q), .clk(in_6));  // open: clr
  Register #(.width(32)) REGISTER_26 (.D(in_1), .en(decoder_1_out24), .Q(REGISTER_26_q), .clk(in_6));  // open: clr
  Register #(.width(32)) REGISTER_27 (.D(in_1), .en(decoder_1_out25), .Q(REGISTER_27_q), .clk(in_6));  // open: clr
  Register #(.width(32)) REGISTER_28 (.D(in_1), .en(decoder_1_out26), .Q(REGISTER_28_q), .clk(in_6));  // open: clr
  Register #(.width(32)) REGISTER_29 (.D(in_1), .en(decoder_1_out27), .Q(REGISTER_29_q), .clk(in_6));  // open: clr
  Register #(.width(32)) REGISTER_30 (.D(in_1), .en(decoder_1_out28), .Q(REGISTER_30_q), .clk(in_6));  // open: clr
  Register #(.width(32)) REGISTER_31 (.D(in_1), .en(decoder_1_out29), .Q(REGISTER_31_q), .clk(in_6));  // open: clr
  Register #(.width(32)) REGISTER_32 (.D(in_1), .en(decoder_1_out30), .Q(REGISTER_32_q), .clk(in_6));  // open: clr
  Multiplexer #(.select(5), .width(32), .enable("false")) multiplexer_1 (
    .in0({32{1'b0}}), .in1(REGISTER_2_q), .in2(REGISTER_3_q), .in3(REGISTER_4_q), .in4(REGISTER_5_q),
    .in5(REGISTER_6_q), .in6(REGISTER_7_q), .in7(REGISTER_8_q), .in8(REGISTER_9_q), .in9(REGISTER_10_q),
    .in10(REGISTER_11_q), .in11(REGISTER_12_q), .in12(REGISTER_13_q), .in13(REGISTER_14_q),
    .in14(REGISTER_15_q), .in15(REGISTER_16_q), .in16(REGISTER_17_q), .in17(REGISTER_18_q),
    .in18(REGISTER_19_q), .in19(REGISTER_20_q), .in20(REGISTER_21_q), .in21(REGISTER_22_q),
    .in22(REGISTER_23_q), .in23(REGISTER_24_q), .in24(REGISTER_25_q), .in25(REGISTER_26_q),
    .in26(REGISTER_27_q), .in27(REGISTER_28_q), .in28(REGISTER_29_q), .in29(REGISTER_30_q),
    .in30(REGISTER_31_q), .in31(REGISTER_32_q), .out(out_7), .sel(in_2));
  Multiplexer #(.select(5), .width(32), .enable("false")) multiplexer_2 (
    .in0({32{1'b0}}), .in1(REGISTER_2_q), .in2(REGISTER_3_q), .in3(REGISTER_4_q), .in4(REGISTER_5_q),
    .in5(REGISTER_6_q), .in6(REGISTER_7_q), .in7(REGISTER_8_q), .in8(REGISTER_9_q), .in9(REGISTER_10_q),
    .in10(REGISTER_11_q), .in11(REGISTER_12_q), .in12(REGISTER_13_q), .in13(REGISTER_14_q),
    .in14(REGISTER_15_q), .in15(REGISTER_16_q), .in16(REGISTER_17_q), .in17(REGISTER_18_q),
    .in18(REGISTER_19_q), .in19(REGISTER_20_q), .in20(REGISTER_21_q), .in21(REGISTER_22_q),
    .in22(REGISTER_23_q), .in23(REGISTER_24_q), .in24(REGISTER_25_q), .in25(REGISTER_26_q),
    .in26(REGISTER_27_q), .in27(REGISTER_28_q), .in28(REGISTER_29_q), .in29(REGISTER_30_q),
    .in30(REGISTER_31_q), .in31(REGISTER_32_q), .out(out_8), .sel(in_5));
endmodule

module CONTROL (
  input  [6:0] OP_CODE,
  input  [2:0] in_2,
  input  in_3,
  output out_4,
  output out_5,
  output out_6,
  output out_7,
  output [1:0] out_8,
  output out_9,
  output [1:0] out_10,
  output [1:0] out_11,
  output [3:0] out_12
);

  wire type_decode_1_auipc, type_decode_1_branch, type_decode_1_i_type, type_decode_1_jal,
       type_decode_1_jalr, type_decode_1_load, type_decode_1_lui, type_decode_1_r_type, type_decode_1_store;

  TYPE_DECODE type_decode_1 (
    .in_1(OP_CODE), .R_TYPE(type_decode_1_r_type), .I_TYPE(type_decode_1_i_type), .LOAD(type_decode_1_load),
    .JALR(type_decode_1_jalr), .STORE(type_decode_1_store), .BRANCH(type_decode_1_branch),
    .AUIPC(type_decode_1_auipc), .LUI(type_decode_1_lui), .JAL(type_decode_1_jal));
  CONTROL_DECODE control_decode_1 (
    .FN_3(in_2), .FN_7(in_3), .REG_Write(out_4), .Branch_2(out_5), .Store_2(out_6), .Mem_2_Reg(out_7),
    .OPERAND_A(out_8), .OPERAND_B(out_9), .IMM_SELECTOR(out_10), .NEXT_PC(out_11),
    .R_Type(type_decode_1_r_type), .I_Type(type_decode_1_i_type), .Load(type_decode_1_load),
    .JALR(type_decode_1_jalr), .Store(type_decode_1_store), .Branch(type_decode_1_branch),
    .Auipc(type_decode_1_auipc), .Lui(type_decode_1_lui), .JAL(type_decode_1_jal), .OUT_0(out_12[0]),
    .OUT_1(out_12[1]), .OUT_2(out_12[2]), .OUT_3(out_12[3]));
endmodule

module ALU (
  input  [31:0] Operand_A,
  input  [31:0] Operand_B,
  input  [3:0] Alu_Out_Select,
  output Overflow,
  output [31:0] ALU_out
);

  wire comparator_1_lt, comparator_2_lt;
  wire [31:0] adder_1_out, and_1_out, bit_extender_1_out, bit_extender_2_out, or_1_out, shifter_1_out,
       shifter_2_out, shifter_3_out, subtractor_1_out, xor_1_out;

  Adder #(.width(32)) adder_1 (.a(Operand_A), .b(Operand_B), .out(adder_1_out), .cout(Overflow));  // open: cin
  Subtractor #(.width(32)) subtractor_1 (.a(Operand_A), .b(Operand_B), .out(subtractor_1_out));  // open: bin, bout
  Comparator #(.width(32)) comparator_1 (.a(Operand_A), .b(Operand_B), .lt(comparator_1_lt));  // open: gt, eq
  Comparator #(.width(32), .mode("unsigned")) comparator_2 (
    .a(Operand_A), .b(Operand_B), .lt(comparator_2_lt));  // open: gt, eq
  Shifter #(.width(32)) shifter_1 (.in(Operand_A), .\dist (Operand_B[4:0]), .out(shifter_1_out));
  assign xor_1_out = Operand_A ^ Operand_B;  // XOR_Gate xor_1, 32 bits wide
  assign and_1_out = Operand_A & Operand_B;  // AND_Gate and_1, 32 bits wide
  assign or_1_out = Operand_A | Operand_B;  // OR_Gate or_1, 32 bits wide
  Shifter #(.width(32), .shift("ar")) shifter_2 (.in(Operand_A), .\dist (Operand_B[4:0]), .out(shifter_2_out));
  Shifter #(.width(32), .shift("lr")) shifter_3 (.in(Operand_A), .\dist (Operand_B[4:0]), .out(shifter_3_out));
  assign bit_extender_1_out = {{31{comparator_1_lt}}, comparator_1_lt};  // Bit_Extender bit_extender_1
  assign bit_extender_2_out = {{31{comparator_2_lt}}, comparator_2_lt};  // Bit_Extender bit_extender_2
  Multiplexer #(.select(4), .width(32), .enable("false")) multiplexer_1 (
    .in0(adder_1_out), .in1(subtractor_1_out), .in2(and_1_out), .in3(or_1_out), .in4(xor_1_out),
    .in5(shifter_1_out), .in6(shifter_3_out), .in7(bit_extender_1_out), .in8(bit_extender_2_out),
    .in9(shifter_2_out), .in15(Operand_A), .out(ALU_out), .sel(Alu_Out_Select));  // open: in10, in11, in12, in13, in14
endmodule

module BRANCH_SEL (
  input  [31:0] in_1,
  input  [31:0] in_2,
  input  [2:0] in_3,
  output out_4
);

  wire comparator_1_eq, comparator_2_eq, comparator_3_lt, comparator_4_eq, comparator_4_gt, comparator_5_lt,
       comparator_6_eq, comparator_6_gt, not_1_out, or_1_out, or_2_out;

  Comparator #(.width(32)) comparator_1 (.a(in_1), .b(in_2), .eq(comparator_1_eq));  // open: gt, lt
  Comparator #(.width(32)) comparator_2 (.a(in_1), .b(in_2), .eq(comparator_2_eq));  // open: gt, lt
  Comparator #(.width(32)) comparator_3 (.a(in_1), .b(in_2), .lt(comparator_3_lt));  // open: gt, eq
  Comparator #(.width(32)) comparator_4 (.a(in_1), .b(in_2), .gt(comparator_4_gt), .eq(comparator_4_eq));  // open: lt
  Comparator #(.width(32), .mode("unsigned")) comparator_5 (.a(in_1), .b(in_2), .lt(comparator_5_lt));  // open: gt, eq
  Comparator #(.width(32), .mode("unsigned")) comparator_6 (
    .a(in_1), .b(in_2), .gt(comparator_6_gt), .eq(comparator_6_eq));  // open: lt
  or or_1 (or_1_out, comparator_4_gt, comparator_4_eq);
  or or_2 (or_2_out, comparator_6_gt, comparator_6_eq);
  not not_1 (not_1_out, comparator_2_eq);
  Multiplexer #(.select(3), .enable("false")) multiplexer_1 (
    .in0(comparator_1_eq), .in1(not_1_out), .in4(comparator_3_lt), .in5(or_1_out), .in6(comparator_5_lt),
    .in7(or_2_out), .out(out_4), .sel(in_3));  // open: in2, in3
endmodule

module ALU_OP (
  input  R,
  input  I,
  input  LOAD,
  input  STORE,
  input  JAL,
  input  JALR,
  input  AUIPC,
  input  LUI,
  output O1,
  output O2,
  output O3
);

  or or_1 (O1, LUI, AUIPC, JALR, JAL);
  or or_2 (O2, LUI, AUIPC, STORE, LOAD);
  or or_3 (O3, LUI, JALR, STORE, I);

  // Notes on the sheet:
  //   ALU OP
endmodule
